# Fritzing sketch Blink (saved by Fritzing 0.9.1b)
circuit board: 6.88566cm x 5.36311cm
breadboards: 1

parts:
  LED1 = LED - 5mm [color="Red (633nm)" package="5 mm [THT]"]
  Bauteil1 = Arduino Uno (Rev3)

nets:
  N1: LED1.cathode, Bauteil1.GND
  N2: LED1.anode, Bauteil1.D13/SCK

notes:
  FADING

// code stored in the sketch: Untitled3.ino
/*
  Blink
  
  Schaltet eine LED im Rythmus von einer Sekunde an und aus.
  
*/

int led = 13;                   // ganzzahlige Variable led wird deklariert

void setup() {                  // die setup()-Methode wird einmal ausgeführt
  pinMode(led, OUTPUT);     
}

void loop() {                   // die loop()-Methode wird immer wiederholt
  digitalWrite(led, HIGH);      // schaltet die LED ein 
  delay(1000);                  // hält das Programm für 1000 Millisekunden an
  digitalWrite(led, LOW);       // schaltet die LED ab
  delay(1000);                  // hält das Programm für 1000 Millisekunden an
}
