# Fritzing sketch Matrix (saved by Fritzing 0.9.2b)
circuit board: 8.93198cm x 6.1522cm
breadboards: 2

parts:
  R5 = Resistor [tolerance=±5% resistance=220 package=THT]
  R6 = Resistor [tolerance=±5% resistance=220 package=THT]
  R7 = Resistor [tolerance=±5% resistance=220 package=THT]
  R8 = Resistor [tolerance=±5% resistance=220 package=THT]
  R9 = Resistor [tolerance=±5% resistance=220 package=THT]
  R10 = Resistor [tolerance=±5% resistance=220 package=THT]
  R11 = Resistor [tolerance=±5% resistance=220 package=THT]
  R12 = Resistor [tolerance=±5% resistance=220 package=THT]
  Arduino1 = Arduino Uno (Rev3)

nets:
  N1: R5.Pin_0, Arduino1.D13/SCK, Arduino1.A4/SDA
  N2: R6.Pin_0, Arduino1.D10_PWM/SS
  N3: R7.Pin_0, Arduino1.A3
  N4: R8.Pin_0, Arduino1.D8
  N5: R9.Pin_0, Arduino1.D5_PWM
  N6: R10.Pin_0, Arduino1.A2
  N7: R11.Pin_0, Arduino1.D4
  N8: R12.Pin_0, Arduino1.A0

notes:
  MATRIX
